// Logisim project cpu.circ as structural Verilog: 6 circuits, main circuit CPU
module CPU (
  input  [31:0] Instruction,
  input  CLK,
  output [31:0] s0,
  output [31:0] s1,
  output [31:0] t0,
  output [31:0] t1,
  output [31:0] a0,
  output [31:0] ra,
  output [31:0] sp,
  output [31:0] PC
);

  wire beq, blt, MemRW, RegWrEn;
  wire [1:0] Asel, Bsel, Lsel, PCsel, WBsel;
  wire [3:0] Alusel;
  wire [31:0] ALU, Imm, load_1_out, main_1_p5, multiplexer_1_out, multiplexer_2_out, multiplexer_3_out,
       plus_4, regfile_1_r1, regfile_1_r2, WB;

  Multiplexer #(.select(2), .width(32), .enable("false")) multiplexer_1 (
    .in0(plus_4), .in1(ALU), .out(multiplexer_1_out), .sel(PCsel));  // open: in2, in3
  // PC pc_1: pin names not known; wires that end beside it: multiplexer_1_out, CLK, PC
  // Incrementer incrementer_1: pin names not known; wires that end beside it: PC, plus_4
  control control_1 (
    .WB(WBsel), .Asel(Asel), .RW(RegWrEn), .Brun(Instruction[13]), .Inst(Instruction), .PCsel(PCsel),
    .Bsel(Bsel), .MEMRW(MemRW), .ALUs(Alusel), .LoadSel(Lsel));
  RegFile regfile_1 (
    .Clk(CLK), .R1(regfile_1_r1), .R2(regfile_1_r2), .WE(RegWrEn), .W(WB), .RD(Instruction[11:7]),
    .RS1(Instruction[19:15]), .RS2(Instruction[24:20]), .s0(s0), .s1(s1), .t0(t0), .t1(t1), .a0(a0), .ra(ra),
    .sp(sp));
  ImmGenerator ImmGenerator (.PC(Instruction), .imm(Imm));
  BComparator bcomparator_1 (.A(regfile_1_r1), .beq(beq), .blt(blt), .B(regfile_1_r2), .bun(Instruction[13]));
  Multiplexer #(.select(2), .width(32), .enable("false")) multiplexer_2 (
    .in0(regfile_1_r1), .in1(PC), .out(multiplexer_2_out), .sel(Asel));  // open: in2, in3
  Multiplexer #(.select(2), .width(32), .enable("false")) multiplexer_3 (
    .in0(regfile_1_r2), .in1(Imm), .out(multiplexer_3_out), .sel(Bsel));  // open: in2, in3
  ALU alu_1 (.A(multiplexer_2_out), .B(multiplexer_3_out), .ALU_Op(Alusel), .Out(ALU));
  Load load_1 (.In(ALU), .out(load_1_out), .LSel(Lsel));
  // memory_main main_1: pin names not known; wires that end beside it: load_1_out, MemRW, regfile_1_r2, CLK, main_1_p5
  Multiplexer #(.select(2), .width(32), .enable("false")) multiplexer_4 (
    .in0(main_1_p5), .in1(ALU), .in2(plus_4), .in3(Imm), .out(WB), .sel(WBsel));

  // Other names for the same wires on the sheet: fetch_addr[31:0] = PC; INST[31:0] = Instruction;
  //   rd[4:0] = Instruction[11:7]; bun = Instruction[13]; rs1[4:0] = Instruction[19:15];
  //   rs2[4:0] = Instruction[24:20]

  // Notes on the sheet:
  //   NOTE
  //   Please do not modify/replace/move/change/delete/etc input and output pins
  //   These are debug/test outputs from your circuit
endmodule

module ImmGenerator (
  input  [31:0] PC,
  output [31:0] imm
);

  wire comparator_1_eq, comparator_2_eq, comparator_3_eq, comparator_4_eq, comparator_5_eq, comparator_6_eq,
       comparator_7_eq, comparator_8_eq, or_1_out, or_2_out;
  wire [2:0] and_1_out, and_2_out, and_3_out, and_4_out, and_5_out, bit_extender_1_out, bit_extender_2_out,
       bit_extender_3_out, bit_extender_4_out, bit_extender_9_out, s_t;
  wire [31:0] B, I, J, S;

  Multiplexer #(.select(3), .width(32), .enable("false")) multiplexer_1 (
    .in1(I), .in2(S), .in3(B), .in4({PC[31:12], {12{1'b0}}}), .in5(J), .out(imm), .sel(s_t));  // open: in0, in6, in7
  Comparator #(.width(7)) comparator_1 (.a(PC[6:0]), .b(7'b0000011), .eq(comparator_1_eq));  // open: gt, lt
  Comparator #(.width(7)) comparator_2 (.a(PC[6:0]), .b(7'b0010011), .eq(comparator_2_eq));  // open: gt, lt
  Comparator #(.width(7)) comparator_3 (.a(PC[6:0]), .b(7'b1100111), .eq(comparator_3_eq));  // open: gt, lt
  Comparator #(.width(7)) comparator_4 (.a(PC[6:0]), .b(7'b0100011), .eq(comparator_4_eq));  // open: gt, lt
  Comparator #(.width(7)) comparator_5 (.a(PC[6:0]), .b(7'b1100011), .eq(comparator_5_eq));  // open: gt, lt
  Comparator #(.width(7)) comparator_6 (.a(PC[6:0]), .b(7'b0110111), .eq(comparator_6_eq));  // open: gt, lt
  Comparator #(.width(7)) comparator_7 (.a(PC[6:0]), .b(7'b0010111), .eq(comparator_7_eq));  // open: gt, lt
  Comparator #(.width(7)) comparator_8 (.a(PC[6:0]), .b(7'b1101111), .eq(comparator_8_eq));  // open: gt, lt
  or or_1 (or_1_out, comparator_6_eq, comparator_7_eq);
  or or_2 (or_2_out, comparator_1_eq, comparator_2_eq, comparator_3_eq);
  assign bit_extender_1_out = {{2{1'b0}}, comparator_4_eq};  // Bit_Extender bit_extender_1
  assign bit_extender_2_out = {{2{1'b0}}, comparator_5_eq};  // Bit_Extender bit_extender_2
  assign bit_extender_3_out = {{2{1'b0}}, or_1_out};  // Bit_Extender bit_extender_3
  assign bit_extender_4_out = {{2{1'b0}}, comparator_8_eq};  // Bit_Extender bit_extender_4
  assign I = {{20{1'b0}}, PC[31:20]};  // Bit_Extender bit_extender_5
  assign S = {{20{1'b0}}, {PC[31:25], PC[11:7]}};  // Bit_Extender bit_extender_6
  assign B = {{19{PC[31]}}, {PC[31], PC[7], PC[30:25], PC[11:8], 1'b0}};  // Bit_Extender bit_extender_7
  assign J = {{11{1'b0}}, {PC[31], PC[19:12], PC[20], PC[30:21], 1'b0}};  // Bit_Extender bit_extender_8
  assign bit_extender_9_out = {{2{1'b0}}, or_2_out};  // Bit_Extender bit_extender_9
  assign and_1_out = bit_extender_1_out & 3'b010;  // AND_Gate and_1, 3 bits wide
  assign and_2_out = bit_extender_2_out & 3'b011;  // AND_Gate and_2, 3 bits wide
  assign and_3_out = bit_extender_3_out & 3'b100;  // AND_Gate and_3, 3 bits wide
  assign and_4_out = bit_extender_4_out & 3'b101;  // AND_Gate and_4, 3 bits wide
  assign and_5_out = bit_extender_9_out & 3'b001;  // AND_Gate and_5, 3 bits wide
  assign s_t = and_5_out | and_1_out | and_2_out | and_3_out | and_4_out;  // OR_Gate or_3, 3 bits wide

  // Other names for the same wires on the sheet: opcode[6:0] = PC[6:0]; U[31:12] = PC[31:12]
endmodule

module BComparator (
  input  [31:0] A,
  input  [31:0] B,
  input  bun,
  output beq,
  output blt
);

  wire comparator_1_eq, comparator_1_lt, comparator_2_eq, comparator_2_lt;

  Comparator #(.width(32)) comparator_1 (.a(A), .b(B), .eq(comparator_1_eq), .lt(comparator_1_lt));  // open: gt
  Comparator #(.width(32)) comparator_2 (.a(A), .b(B), .eq(comparator_2_eq), .lt(comparator_2_lt));  // open: gt
  Multiplexer multiplexer_1 (.in0(comparator_1_eq), .in1(comparator_2_eq), .out(beq), .sel(bun));  // open: en
  Multiplexer multiplexer_2 (.in0(comparator_1_lt), .in1(comparator_2_lt), .out(blt), .sel(bun));  // open: en
endmodule

module control (
  input  [31:0] Inst,
  output [1:0] WB,
  output [1:0] Asel,
  output RW,
  output Brun,
  output [1:0] PCsel,
  output [1:0] Bsel,
  output MEMRW,
  output [3:0] ALUs,
  output [1:0] LoadSel
);

  wire [1:0] rom_2_data;
  wire [10:0] multiplexer_1_out;

  ROM #(.addrWidth(7), .dataWidth(11)) rom_1 (
    .addr(Inst[6:0]), .data({WB, PCsel, Asel, Bsel, RW, MEMRW, Brun}), .sel(1'b1));
  ROM #(.addrWidth(7), .dataWidth(2)) rom_2 (.addr(Inst[6:0]), .data(rom_2_data), .sel(1'b1));
  Multiplexer #(.select(2), .width(11), .enable("false")) multiplexer_1 (
    .in0({Inst[14:12], 1'b0, Inst[31:25]}), .in1({Inst[14:12], {8{1'b0}}}), .in2({Inst[14:12], 8'hf}),
    .in3(11'hf), .out(multiplexer_1_out), .sel(rom_2_data));
  ROM #(.addrWidth(11), .dataWidth(4)) rom_3 (.addr(multiplexer_1_out), .data(ALUs), .sel(1'b1));

  assign LoadSel = Inst[13:12];

  // Other names for the same wires on the sheet: Br = Brun; MEM = MEMRW; Bs[1:0] = Bsel; As[1:0] = Asel;
  //   PC[1:0] = PCsel; fun7[6:0] = Inst[31:25]; func3[2:0] = Inst[14:12]; opcode[6:0] = Inst[6:0]

  // Notes on the sheet:
  //   contents of rom_1 (hex, n*v repeats v):
  //   0 0 0 c 15*0 20c 15*0 e 15*0 204 0 0 0 604 43*0 729 0 0 0 48c 7*0 4ac
  //   contents of rom_2 (hex, n*v repeats v):
  //   0 0 0 2 15*0 1 15*0 2 19*0 3 43*0 2 0 0 0 2 7*0 3
  //   contents of rom_3 (hex, n*v repeats v):
  //   2 7 b 12*0 2 16*0 b 224*0 8 13*0 2 240*0 6 14*0 2 496*0 5 9 13*0 2 240*0 1 255*0 4 a 13*0 2 240*0 3
endmodule

module ALUsel (
  input  [31:0] in_1,
  output [3:0] Alusel
);

  wire and_1_out, comparator_6_eq, comparator_11_eq, comparator_12_eq;
  wire [1:0] comparator_4_eq, ControlFunct7;
  wire [2:0] comparator_1_eq;
  wire [3:0] AMS, comparator_7_eq, DSS, I, IFunctSel, multiplexer_3_out, R, RA, RFunctSel, SM;

  Comparator #(.width(7)) comparator_1 (.a(in_1[31:25]), .b({7{1'b0}}), .eq(comparator_1_eq[0]));  // open: gt, lt
  Comparator #(.width(7)) comparator_2 (.a(in_1[31:25]), .b(7'b0000001), .eq(comparator_1_eq[1]));  // open: gt, lt
  Comparator #(.width(7)) comparator_3 (.a(in_1[31:25]), .b(7'b0100000), .eq(comparator_1_eq[2]));  // open: gt, lt
  Multiplexer #(.select(3), .width(4)) multiplexer_1 (
    .in0(4'b0000), .in1(4'b0110), .in2(4'b0111), .in3(4'b1011), .in4(4'b0011), .in5(4'b0101), .in6(4'b0010),
    .in7(4'b0001), .out(RFunctSel), .sel(in_1[14:12]));  // open: en
  Multiplexer #(.select(3), .width(4)) multiplexer_2 (
    .in0(4'b0000), .in1(4'b0110), .in2(4'b0111), .in4(4'b0011), .in5(4'b0101), .in6(4'b0010), .in7(4'b0001),
    .out(IFunctSel), .sel(in_1[14:12]));  // open: in3, en
  Comparator #(.width(7)) comparator_4 (.a(in_1[6:0]), .b(7'b0010011), .eq(comparator_4_eq[0]));  // open: gt, lt
  Comparator #(.width(7)) comparator_5 (.a(in_1[6:0]), .b(7'b0110011), .eq(comparator_4_eq[1]));  // open: gt, lt
  Comparator #(.width(7)) comparator_6 (.a(in_1[6:0]), .b(7'b0110111), .eq(comparator_6_eq));  // open: gt, lt
  Multiplexer #(.select(2), .width(4)) multiplexer_3 (
    .in0(4'b0000), .in1(I), .in2(R), .out(multiplexer_3_out), .sel(comparator_4_eq));  // open: in3, en
  Multiplexer #(.select(3), .width(2)) multiplexer_4 (
    .in1(2'b00), .in2(2'b01), .in4(2'b10), .out(ControlFunct7), .sel(comparator_1_eq));  // open: in0, in3, in5, in6, in7, en
  Multiplexer #(.select(2), .width(4)) multiplexer_5 (
    .in0(4'b0000), .in1(4'b1010), .in2(4'b1100), .out(AMS), .sel(ControlFunct7));  // open: in3, en
  Multiplexer #(.select(2), .width(4)) multiplexer_6 (
    .in0(4'b0110), .in1(4'b1011), .out(SM), .sel(ControlFunct7));  // open: in2, in3, en
  Multiplexer #(.width(4)) multiplexer_7 (
    .in0(multiplexer_3_out), .in1(4'b1101), .out(Alusel), .sel(comparator_6_eq));  // open: en
  Comparator #(.width(4)) comparator_7 (.a(RFunctSel), .b(4'b0000), .eq(comparator_7_eq[0]));  // open: gt, lt
  Comparator #(.width(4)) comparator_8 (.a(RFunctSel), .b(4'b0110), .eq(comparator_7_eq[1]));  // open: gt, lt
  Comparator #(.width(4)) comparator_9 (.a(RFunctSel), .b(4'b0101), .eq(comparator_7_eq[2]));  // open: gt, lt
  Comparator #(.width(4)) comparator_10 (.a(RFunctSel), .b(4'b0001), .eq(comparator_7_eq[3]));  // open: gt, lt
  Comparator #(.width(4)) comparator_11 (.a(IFunctSel), .b(4'b0101), .eq(comparator_11_eq));  // open: gt, lt
  Comparator #(.width(7)) comparator_12 (.a(in_1[31:25]), .b({7{1'b0}}), .eq(comparator_12_eq));  // open: gt, lt
  Multiplexer #(.select(2), .width(4)) multiplexer_8 (
    .in0(4'b0100), .in1(4'b1000), .in2(4'b0101), .out(DSS), .sel(ControlFunct7));  // open: in3, en
  Multiplexer #(.select(2), .width(4)) multiplexer_9 (
    .in0(4'b0001), .in1(4'b1001), .out(RA), .sel(ControlFunct7));  // open: in2, in3, en
  and and_1 (and_1_out, comparator_11_eq, comparator_12_eq);
  Multiplexer #(.select(4), .width(4)) multiplexer_10 (
    .in0(RFunctSel), .in1(AMS), .in2(SM), .in4(DSS), .in8(RA), .out(R), .sel(comparator_7_eq));  // open: in3, in5, in6, in7, in9, in10, in11, in12, in13, in14, in15, en
  Multiplexer #(.width(4)) multiplexer_11 (.in0(IFunctSel), .in1(4'b0100), .out(I), .sel(and_1_out));  // open: en

  // Other names for the same wires on the sheet: opcode[6:0] = in_1[6:0]; funct3[2:0] = in_1[14:12];
  //   funct7[6:0] = in_1[31:25]
endmodule

module Load (
  input  [1:0] LSel,
  input  [31:0] In,
  output [31:0] out
);

  wire [31:0] bit_extender_1_out, bit_extender_2_out;

  assign bit_extender_1_out = {{24{1'b0}}, In[7:0]};  // Bit_Extender bit_extender_1
  assign bit_extender_2_out = {{16{1'b0}}, In[15:0]};  // Bit_Extender bit_extender_2
  Multiplexer #(.select(2), .width(32), .enable("false")) multiplexer_1 (
    .in0(bit_extender_1_out), .in1(bit_extender_2_out), .in2(In), .out(out), .sel(LSel));  // open: in3
endmodule
